# Fritzing sketch NFCYoklama Şema (saved by Fritzing 0.9.10b)

parts:
  T3_Vakfı1 = Generic shrouded header - 32 pins [package=THT]
  Parça1 = RFID-RC522v3
  Nokia_5110_LCD_Module1 = Nokia 5110 LCD

nets:
  N1: T3_Vakfı1.pin10, Nokia_5110_LCD_Module1.Din
  N2: T3_Vakfı1.pin11, Nokia_5110_LCD_Module1.D/C
  N3: T3_Vakfı1.pin12, Nokia_5110_LCD_Module1.CE
  N4: T3_Vakfı1.pin13, Nokia_5110_LCD_Module1.RST
  N5: T3_Vakfı1.pin16, Nokia_5110_LCD_Module1.GND
  N6: T3_Vakfı1.pin17, Parça1.connector13
  N7: T3_Vakfı1.pin18, Parça1.connector15, Nokia_5110_LCD_Module1.VCC
  N8: T3_Vakfı1.pin21, Parça1.connector8
  N9: T3_Vakfı1.pin24, Parça1.connector10
  N10: T3_Vakfı1.pin25, Parça1.connector11
  N11: T3_Vakfı1.pin26, Parça1.connector9
  N12: T3_Vakfı1.pin30, Nokia_5110_LCD_Module1.CLK
  N13: T3_Vakfı1.pin31, Parça1.connector14

custom parts:
  Generic shrouded header - 32 pins: Ülkemizin mühendislik kaynakları kullanılarak geliştirilen Deneyap Kart; güçlü işlemcisi, dayanıklı tasarımı ve çok yönlü giriş/çıkış pinleri ile kullanıcılara Elektronik Programlama, Nesnelerin İnterneti (IoT) ve Yapay Zeka alanlarında başlangıç seviyesinden endüstriyel uygulamalara kadar her seviyede projeyi yapma imkanı sunuyor.
  Nokia 5110 LCD: Nokia 5110 Graphic 84*48 LCD module <Blue Version>
